# Fritzing sketch Untitled Sketch (saved by Fritzing 0.9.3b)
breadboards: 1

parts:
  Part1 = Arduino Uno (Rev3)
  DRV_1 = DRV 8825 Stepper Motor Carrier, High Current [part_number="DRV 8825"]
  S1 = Pushbutton [package="[THT]"]
  R1 = Resistor [tolerance=±5% resistance=10k package=THT]
  C1 = Electrolytic Capacitor [capacitance=0.1mF voltage=20V package="100 mil [THT, electrolytic]"]
  M1 = Stepper Motor - Bipolar

nets:
  N1: Part1.D8, DRV_1.DIRECTION
  N2: Part1.D9_PWM, DRV_1.STEP
  N3: Part1.D12/MISO, DRV_1.ENABLE
  N4: Part1.GND, DRV_1.GROUND_LOG, R1.Pin_1, C1.+
  N5: Part1.D7, Part1.5V, DRV_1.MS1, S1.Pin_1, S1.Pin_2, S1.Pin_3, S1.Pin_4, R1.Pin_0
  N6: DRV_1.OUT_2B, M1.A
  N7: DRV_1.OUT_2A, M1.C
  N8: DRV_1.OUT_1A, M1.B
  N9: DRV_1.OUT_1B, M1.D
